# Fritzing sketch breadboard (saved by Fritzing 1.0.2b)
breadboards: 1

parts:
  M2 = gear-motor [mn=2]
  M3 = gear-motor [mn=2]
  Mod1 = Raspberry Pi 4B
  IC1 = L293D [package=THT]
  VCC1 = Battery
  Part1 = Breadboard Power Supply Board SMD
  VCC2 = Battery block 9V  # not connected

nets:
  N1: M2.pin_1, IC1.Out_1_(_Controlled_by_Enable_1_)
  N2: M2.pin_2, IC1.Out_2_(_Controlled_by_Enable_1_)
  N3: M3.pin_1, IC1.Out_3_(_Controlled_by_Enable_2_)
  N4: M3.pin_2, IC1.Out_4_(_Controlled_by_Enable_2_)
  N5: Mod1.3V3, IC1.+V
  GND: Mod1.GND, IC1.0V, VCC1.-, Part1.GND
  N6: Mod1.GPIO23, IC1.Enable_2
  N7: Mod1.GPIO24, IC1.In_3
  N8: Mod1.GPIO8, IC1.In_4
  N9: Mod1.GPIO5, IC1.Enable_1
  N10: Mod1.GPIO6, IC1.In_1
  N11: Mod1.GPIO13, IC1.In_2
  N12: IC1.+Vmotor, VCC1.+, Part1.VCC
